// Digital circuit Simplic-Refactor.dig as structural Verilog
module Simplic_Refactor (
  input  [15:0] in_1,
  input  in_2,
  input  clk,
  input  [15:0] BSP,
  input  in_5,
  input  [7:0] in_6
);

  wire A_en, and_1_out, B_en;
  wire [1:0] Mode;
  wire [3:0] Opcode;
  wire [9:0] Imm10;
  wire [15:0] A, Address, B, C_q, PC;

  ROM #(.bigEndian("true"), .AddrBits(16), .Bits(16)) INSTR (.A(PC), .sel(1'b1), .D({Opcode, Mode, Imm10}));
  and and_1 (and_1_out, Opcode[0], Opcode[1], ~Opcode[2], ~Opcode[3]);  // And
  and and_2 (B_en, ~Opcode[0], Opcode[1], ~Opcode[2], ~Opcode[3]);  // And
  EEPROMDualPort #(.AddrBits(16), .Bits(8)) MEM (.A(Address), .Din(in_6), .str(1'b0), .C(1'b0), .ld(1'b0));  // open: D
  Add #(.Bits(16)) add_1 (.a(A), .b({{6{1'b0}}, Imm10}), .c_i(1'b0), .s(Address));  // open: c_o
  // Probe on Imm10
  // Probe on Mode
  // Probe on Opcode
  or or_1 (A_en, and_1_out, B_en);
  Add #(.Bits(16)) add_2 (.a(A), .b({{6{1'b0}}, Imm10}), .c_i(1'b0), .s(Address));  // open: c_o
  Register #(.Bits(16)) u_A (.D({{6{1'b0}}, Imm10}), .C(clk), .en(A_en), .Q(A));
  Register #(.Bits(16)) u_B (.D(A), .C(clk), .en(B_en), .Q(B));
  Register #(.Bits(16)) C (.D(B), .C(clk), .en(1'b0), .Q(C_q));
  Register #(.Bits(16)) u_BSP (.D(BSP), .C(clk), .en(in_5));  // open: Q
  CounterPreset #(.Bits(16)) u_PC (
    .en(1'b1), .C(clk), .dir(1'b0), .in(in_1), .ld(in_2), .clr(1'b0), .out(PC));  // open: ovf
  // Probe on A
  // Probe on B
  // Probe on C_q

  // Other names for the same wires on the sheet: Result[7:0] = in_6

  // Notes on the sheet:
  //   contents of INSTR (hex, n*v repeats v):
  //   3123,2321,2000,2000
  //   contents of MEM (hex, n*v repeats v):
  //   b520
  //   INS
  //   PUSH
endmodule
